# Fritzing sketch raspi-flask-iot-schematics (saved by Fritzing 0.9.3b)
breadboards: 1

parts:
  Raspberry_Pi_1 = Raspberry Pi 3 [part_number=RPI-3-V1.2]
  DHT1 = DHT11 Humitidy and Temperature Sensor
  LED2 = smd LED [color="Red (633nm)" package="0805 [SMD]"]
  LED3 = smd LED [color="Orange (620nm)" package="0603 [SMD]"]

nets:
  3V3: Raspberry_Pi_1.3v3, DHT1.VDD
  GND: Raspberry_Pi_1.GND, DHT1.GND, LED2.cathode, LED3.cathode
  N1: Raspberry_Pi_1.GIPO20, LED3.anode
  N2: Raspberry_Pi_1.GIPO12, LED2.anode
  N3: Raspberry_Pi_1.GIPO24, DHT1.DATA

notes:
  DHT connected to GPIO 24
  RED LED connected to GPIO 12
  ORANGE LED connected to GPIO 20

custom parts:
  DHT11 Humitidy and Temperature Sensor: DHT11 Humidity and Temperature Sensor
